# Fritzing sketch Untitled Sketch (saved by Fritzing 1.0.2b)

parts:
  U1 = LuaNode32 / ESP32 [part_number=ESP32S-PIN30]
  S1 = H-Bridge with L298N
  HC-SR04_Sensor_1 = HC-SR04 Ultrasonic Distance Sensor
  U2 = SWITCH-SPST-2 [package=switch-spst-vertical]
  M5 = DC Motor [voltage_(max)=6V voltage_(min)=3V]
  VCC1 = Battery
  M6 = DC Motor [voltage_(max)=6V voltage_(min)=3V]
  Izquierdo = KY-033 Tracing Black White Line Hunting Sensor Module For Arduino
  Derecho = KY-033 Tracing Black White Line Hunting Sensor Module For Arduino

nets:
  N1: U1.D34, Derecho.S
  N2: U1.D35, Izquierdo.S
  N3: U1.D26, S1.IN4
  N4: U1.D27, S1.IN3
  N5: U1.D14, S1.IN2
  N6: U1.D12, S1.IN1
  GND: U1.GND, S1.GND, HC-SR04_Sensor_1.GND, VCC1.-
  VIN: U1.Vin, S1.5V
  3V3: U1.3V3, HC-SR04_Sensor_1.VCC
  N7: U1.D2, HC-SR04_Sensor_1.ECHO
  N8: U1.D4, HC-SR04_Sensor_1.TRIG
  N9: U1.D5, S1.ENB
  N10: U1.D18, S1.ENA
  N11: S1.12V, U2.O
  N12: S1.M1-01, M5.pin_2
  N13: S1.M1-02, M5.pin_1
  N14: S1.M2-01, M6.pin_2
  N15: S1.M2-02, M6.pin_1
  N16: U2.P, VCC1.+

custom parts:
  LuaNode32 / ESP32: New Image for LuaNode32 DOIT ESP32 DEVKIT V1. Base parts from LuaNode32 / ESP32 ESP32 based LuaNode32 by G.Noorlander DOIT Esp32 DevKit v1 (30 pins long, 11 pins width) by Werner Rothschopf (modified by vanepp Dec 2018)
  H-Bridge with L298N: h-bridge
  Battery: Your standard 2x 18650 battery pack (7.4 Volts)
  KY-033 Tracing Black White Line Hunting Sensor Module For Arduino: Tracing Black White Line Hunting Sensor Module For Arduino Description: This is KY-033 tracking sensor. The KY-033 measures the intensity of infrared radiation and delivers it as an analog output voltage. Features: Operating voltage: 2.5 - 12V(cannot over12V) working current: 18mA-20mA at 5V Enhanced accuracy Documents: http://www.vishay.com/docs/83760/tcrt5000.pdf
